// Logisim project regfile.circ as structural Verilog: 2 circuits, main circuit regfile
module regfile (
  input  [4:0] rs1,
  input  [4:0] rs2,
  input  [4:0] rd,
  input  [31:0] Write_Data,
  input  RegWEn,
  input  clk,
  output [31:0] ra,
  output [31:0] sp,
  output [31:0] t0,
  output [31:0] t1,
  output [31:0] t2,
  output [31:0] s0,
  output [31:0] s1,
  output [31:0] a0,
  output [31:0] Read_Data_1,
  output [31:0] Read_Data_2
);

  wire regdatainput_1_writeflag, regdatainput_2_writeflag, regdatainput_3_writeflag,
       regdatainput_4_writeflag, regdatainput_5_writeflag, regdatainput_6_writeflag,
       regdatainput_7_writeflag, regdatainput_8_writeflag, regdatainput_9_writeflag,
       regdatainput_10_writeflag, regdatainput_11_writeflag, regdatainput_12_writeflag,
       regdatainput_13_writeflag, regdatainput_14_writeflag, regdatainput_15_writeflag,
       regdatainput_16_writeflag, regdatainput_17_writeflag, regdatainput_18_writeflag,
       regdatainput_19_writeflag, regdatainput_20_writeflag, regdatainput_21_writeflag,
       regdatainput_22_writeflag, regdatainput_23_writeflag, regdatainput_24_writeflag,
       regdatainput_25_writeflag, regdatainput_26_writeflag, regdatainput_27_writeflag,
       regdatainput_28_writeflag, regdatainput_29_writeflag, regdatainput_30_writeflag,
       regdatainput_31_writeflag, write1, write2, write3, write4, write5, write6, write7, write8, write9,
       write10, write11, write12, write13, write14, write15, write16, write17, write18, write19, write20,
       write21, write22, write23, write24, write25, write26, write27, write28, write29, write30, write31;
  wire [31:0] inx1, inx2, inx3, inx4, inx5, inx6, inx7, inx8, inx9, inx10, inx11, inx12, inx13, inx14, inx15,
       inx16, inx17, inx18, inx19, inx20, inx21, inx22, inx23, inx24, inx25, inx26, inx27, inx28, inx29,
       inx30, inx31, outx0, outx3, outx4, outx11, outx12, outx13, outx14, outx15, outx16, outx17, outx18,
       outx19, outx20, outx21, outx22, outx23, outx24, outx25, outx26, outx27, outx28, outx29, outx30,
       outx31, regdatainput_1_data_out, regdatainput_2_data_out, regdatainput_3_data_out,
       regdatainput_4_data_out, regdatainput_5_data_out, regdatainput_6_data_out, regdatainput_7_data_out,
       regdatainput_8_data_out, regdatainput_9_data_out, regdatainput_10_data_out, regdatainput_11_data_out,
       regdatainput_12_data_out, regdatainput_13_data_out, regdatainput_14_data_out,
       regdatainput_15_data_out, regdatainput_16_data_out, regdatainput_17_data_out,
       regdatainput_18_data_out, regdatainput_19_data_out, regdatainput_20_data_out,
       regdatainput_21_data_out, regdatainput_22_data_out, regdatainput_23_data_out,
       regdatainput_24_data_out, regdatainput_25_data_out, regdatainput_26_data_out,
       regdatainput_27_data_out, regdatainput_28_data_out, regdatainput_29_data_out,
       regdatainput_30_data_out, regdatainput_31_data_out;

  Register #(.width(32)) x0 (.D({32{1'b0}}), .clk(clk), .Q(outx0));  // open: en, clr
  Register #(.width(32)) x1 (
    .D(regdatainput_1_data_out), .en(regdatainput_1_writeflag), .clk(clk), .Q(ra));  // open: clr
  regdatainput regdatainput_1 (
    .data_in(inx1), .write_en(write1), .data_out(regdatainput_1_data_out),
    .writeflag(regdatainput_1_writeflag));
  Register #(.width(32)) x2 (
    .D(regdatainput_2_data_out), .en(regdatainput_2_writeflag), .clk(clk), .Q(sp));  // open: clr
  regdatainput regdatainput_2 (
    .data_in(inx2), .write_en(write2), .data_out(regdatainput_2_data_out),
    .writeflag(regdatainput_2_writeflag));
  Register #(.width(32)) x3 (
    .D(regdatainput_3_data_out), .en(regdatainput_3_writeflag), .clk(clk), .Q(outx3));  // open: clr
  regdatainput regdatainput_3 (
    .data_in(inx3), .write_en(write3), .data_out(regdatainput_3_data_out),
    .writeflag(regdatainput_3_writeflag));
  Register #(.width(32)) x4 (
    .D(regdatainput_4_data_out), .en(regdatainput_4_writeflag), .clk(clk), .Q(outx4));  // open: clr
  regdatainput regdatainput_4 (
    .data_in(inx4), .write_en(write4), .data_out(regdatainput_4_data_out),
    .writeflag(regdatainput_4_writeflag));
  Register #(.width(32)) x5 (
    .D(regdatainput_5_data_out), .en(regdatainput_5_writeflag), .clk(clk), .Q(t0));  // open: clr
  regdatainput regdatainput_5 (
    .data_in(inx5), .write_en(write5), .data_out(regdatainput_5_data_out),
    .writeflag(regdatainput_5_writeflag));
  Register #(.width(32)) x6 (
    .D(regdatainput_6_data_out), .en(regdatainput_6_writeflag), .clk(clk), .Q(t1));  // open: clr
  regdatainput regdatainput_6 (
    .data_in(inx6), .write_en(write6), .data_out(regdatainput_6_data_out),
    .writeflag(regdatainput_6_writeflag));
  Register #(.width(32)) x7 (
    .D(regdatainput_7_data_out), .en(regdatainput_7_writeflag), .clk(clk), .Q(t2));  // open: clr
  regdatainput regdatainput_7 (
    .data_in(inx7), .write_en(write7), .data_out(regdatainput_7_data_out),
    .writeflag(regdatainput_7_writeflag));
  Register #(.width(32)) x8 (
    .D(regdatainput_8_data_out), .en(regdatainput_8_writeflag), .clk(clk), .Q(s0));  // open: clr
  regdatainput regdatainput_8 (
    .data_in(inx8), .write_en(write8), .data_out(regdatainput_8_data_out),
    .writeflag(regdatainput_8_writeflag));
  // Probe on rd
  // Probe on Write_Data
  Demultiplexer #(.enable("false"), .select(5), .width(32)) demultiplexer_1 (
    .out1(inx1), .out2(inx2), .out3(inx3), .out4(inx4), .out5(inx5), .out6(inx6), .out7(inx7), .out8(inx8),
    .out9(inx9), .out10(inx10), .out11(inx11), .out12(inx12), .out13(inx13), .out14(inx14), .out15(inx15),
    .out16(inx16), .out17(inx17), .out18(inx18), .out19(inx19), .out20(inx20), .out21(inx21), .out22(inx22),
    .out23(inx23), .out24(inx24), .out25(inx25), .out26(inx26), .out27(inx27), .out28(inx28), .out29(inx29),
    .out30(inx30), .out31(inx31), .in(Write_Data), .sel(rd));  // open: out0
  Register #(.width(32)) x9 (
    .D(regdatainput_9_data_out), .en(regdatainput_9_writeflag), .clk(clk), .Q(s1));  // open: clr
  regdatainput regdatainput_9 (
    .data_in(inx9), .write_en(write9), .data_out(regdatainput_9_data_out),
    .writeflag(regdatainput_9_writeflag));
  Register #(.width(32)) x10 (
    .D(regdatainput_10_data_out), .en(regdatainput_10_writeflag), .clk(clk), .Q(a0));  // open: clr
  regdatainput regdatainput_10 (
    .data_in(inx10), .write_en(write10), .data_out(regdatainput_10_data_out),
    .writeflag(regdatainput_10_writeflag));
  Register #(.width(32)) x11 (
    .D(regdatainput_11_data_out), .en(regdatainput_11_writeflag), .clk(clk), .Q(outx11));  // open: clr
  regdatainput regdatainput_11 (
    .data_in(inx11), .write_en(write11), .data_out(regdatainput_11_data_out),
    .writeflag(regdatainput_11_writeflag));
  Register #(.width(32)) x12 (
    .D(regdatainput_12_data_out), .en(regdatainput_12_writeflag), .clk(clk), .Q(outx12));  // open: clr
  regdatainput regdatainput_12 (
    .data_in(inx12), .write_en(write12), .data_out(regdatainput_12_data_out),
    .writeflag(regdatainput_12_writeflag));
  Register #(.width(32)) x13 (
    .D(regdatainput_13_data_out), .en(regdatainput_13_writeflag), .clk(clk), .Q(outx13));  // open: clr
  regdatainput regdatainput_13 (
    .data_in(inx13), .write_en(write13), .data_out(regdatainput_13_data_out),
    .writeflag(regdatainput_13_writeflag));
  Register #(.width(32)) x14 (
    .D(regdatainput_14_data_out), .en(regdatainput_14_writeflag), .clk(clk), .Q(outx14));  // open: clr
  regdatainput regdatainput_14 (
    .data_in(inx14), .write_en(write14), .data_out(regdatainput_14_data_out),
    .writeflag(regdatainput_14_writeflag));
  Register #(.width(32)) x15 (
    .D(regdatainput_15_data_out), .en(regdatainput_15_writeflag), .clk(clk), .Q(outx15));  // open: clr
  regdatainput regdatainput_15 (
    .data_in(inx15), .write_en(write15), .data_out(regdatainput_15_data_out),
    .writeflag(regdatainput_15_writeflag));
  Register #(.width(32)) x16 (
    .D(regdatainput_16_data_out), .en(regdatainput_16_writeflag), .clk(clk), .Q(outx16));  // open: clr
  regdatainput regdatainput_16 (
    .data_in(inx16), .write_en(write16), .data_out(regdatainput_16_data_out),
    .writeflag(regdatainput_16_writeflag));
  Register #(.width(32)) x17 (
    .D(regdatainput_17_data_out), .en(regdatainput_17_writeflag), .clk(clk), .Q(outx17));  // open: clr
  regdatainput regdatainput_17 (
    .data_in(inx17), .write_en(write17), .data_out(regdatainput_17_data_out),
    .writeflag(regdatainput_17_writeflag));
  Register #(.width(32)) x18 (
    .D(regdatainput_18_data_out), .en(regdatainput_18_writeflag), .clk(clk), .Q(outx18));  // open: clr
  regdatainput regdatainput_18 (
    .data_in(inx18), .write_en(write18), .data_out(regdatainput_18_data_out),
    .writeflag(regdatainput_18_writeflag));
  Register #(.width(32)) x19 (
    .D(regdatainput_19_data_out), .en(regdatainput_19_writeflag), .clk(clk), .Q(outx19));  // open: clr
  regdatainput regdatainput_19 (
    .data_in(inx19), .write_en(write19), .data_out(regdatainput_19_data_out),
    .writeflag(regdatainput_19_writeflag));
  Register #(.width(32)) x20 (
    .D(regdatainput_20_data_out), .en(regdatainput_20_writeflag), .clk(clk), .Q(outx20));  // open: clr
  regdatainput regdatainput_20 (
    .data_in(inx20), .write_en(write20), .data_out(regdatainput_20_data_out),
    .writeflag(regdatainput_20_writeflag));
  Register #(.width(32)) x21 (
    .D(regdatainput_21_data_out), .en(regdatainput_21_writeflag), .clk(clk), .Q(outx21));  // open: clr
  regdatainput regdatainput_21 (
    .data_in(inx21), .write_en(write21), .data_out(regdatainput_21_data_out),
    .writeflag(regdatainput_21_writeflag));
  Register #(.width(32)) x22 (
    .D(regdatainput_22_data_out), .en(regdatainput_22_writeflag), .clk(clk), .Q(outx22));  // open: clr
  regdatainput regdatainput_22 (
    .data_in(inx22), .write_en(write22), .data_out(regdatainput_22_data_out),
    .writeflag(regdatainput_22_writeflag));
  Register #(.width(32)) x23 (
    .D(regdatainput_23_data_out), .en(regdatainput_23_writeflag), .clk(clk), .Q(outx23));  // open: clr
  regdatainput regdatainput_23 (
    .data_in(inx23), .write_en(write23), .data_out(regdatainput_23_data_out),
    .writeflag(regdatainput_23_writeflag));
  Register #(.width(32)) x24 (
    .D(regdatainput_24_data_out), .en(regdatainput_24_writeflag), .clk(clk), .Q(outx24));  // open: clr
  regdatainput regdatainput_24 (
    .data_in(inx24), .write_en(write24), .data_out(regdatainput_24_data_out),
    .writeflag(regdatainput_24_writeflag));
  Multiplexer #(.enable("false"), .select(5), .width(32)) multiplexer_1 (
    .in0(outx0), .in1(ra), .in2(sp), .in3(outx3), .in4(outx4), .in5(t0), .in6(t1), .in7(t2), .in8(s0),
    .in9(s1), .in10(a0), .in11(outx11), .in12(outx12), .in13(outx13), .in14(outx14), .in15(outx15),
    .in16(outx16), .in17(outx17), .in18(outx18), .in19(outx19), .in20(outx20), .in21(outx21), .in22(outx22),
    .in23(outx23), .in24(outx24), .in25(outx25), .in26(outx26), .in27(outx27), .in28(outx28), .in29(outx29),
    .in30(outx30), .in31(outx31), .out(Read_Data_1), .sel(rs1));
  Register #(.width(32)) x25 (
    .D(regdatainput_25_data_out), .en(regdatainput_25_writeflag), .clk(clk), .Q(outx25));  // open: clr
  regdatainput regdatainput_25 (
    .data_in(inx25), .write_en(write25), .data_out(regdatainput_25_data_out),
    .writeflag(regdatainput_25_writeflag));
  Register #(.width(32)) x26 (
    .D(regdatainput_26_data_out), .en(regdatainput_26_writeflag), .clk(clk), .Q(outx26));  // open: clr
  regdatainput regdatainput_26 (
    .data_in(inx26), .write_en(write26), .data_out(regdatainput_26_data_out),
    .writeflag(regdatainput_26_writeflag));
  Register #(.width(32)) x27 (
    .D(regdatainput_27_data_out), .en(regdatainput_27_writeflag), .clk(clk), .Q(outx27));  // open: clr
  regdatainput regdatainput_27 (
    .data_in(inx27), .write_en(write27), .data_out(regdatainput_27_data_out),
    .writeflag(regdatainput_27_writeflag));
  Register #(.width(32)) x28 (
    .D(regdatainput_28_data_out), .en(regdatainput_28_writeflag), .clk(clk), .Q(outx28));  // open: clr
  regdatainput regdatainput_28 (
    .data_in(inx28), .write_en(write28), .data_out(regdatainput_28_data_out),
    .writeflag(regdatainput_28_writeflag));
  Register #(.width(32)) x29 (
    .D(regdatainput_29_data_out), .en(regdatainput_29_writeflag), .clk(clk), .Q(outx29));  // open: clr
  regdatainput regdatainput_29 (
    .data_in(inx29), .write_en(write29), .data_out(regdatainput_29_data_out),
    .writeflag(regdatainput_29_writeflag));
  Register #(.width(32)) x30 (
    .D(regdatainput_30_data_out), .en(regdatainput_30_writeflag), .clk(clk), .Q(outx30));  // open: clr
  regdatainput regdatainput_30 (
    .data_in(inx30), .write_en(write30), .data_out(regdatainput_30_data_out),
    .writeflag(regdatainput_30_writeflag));
  Register #(.width(32)) x31 (
    .D(regdatainput_31_data_out), .en(regdatainput_31_writeflag), .clk(clk), .Q(outx31));  // open: clr
  regdatainput regdatainput_31 (
    .data_in(inx31), .write_en(write31), .data_out(regdatainput_31_data_out),
    .writeflag(regdatainput_31_writeflag));
  Multiplexer #(.enable("false"), .select(5), .width(32)) multiplexer_2 (
    .in0(outx0), .in1(ra), .in2(sp), .in3(outx3), .in4(outx4), .in5(t0), .in6(t1), .in7(t2), .in8(s0),
    .in9(s1), .in10(a0), .in11(outx11), .in12(outx12), .in13(outx13), .in14(outx14), .in15(outx15),
    .in16(outx16), .in17(outx17), .in18(outx18), .in19(outx19), .in20(outx20), .in21(outx21), .in22(outx22),
    .in23(outx23), .in24(outx24), .in25(outx25), .in26(outx26), .in27(outx27), .in28(outx28), .in29(outx29),
    .in30(outx30), .in31(outx31), .out(Read_Data_2), .sel(rs2));
  // Probe on RegWEn
  Demultiplexer #(.enable("false"), .select(5)) demultiplexer_2 (
    .out1(write1), .out2(write2), .out3(write3), .out4(write4), .out5(write5), .out6(write6), .out7(write7),
    .out8(write8), .out9(write9), .out10(write10), .out11(write11), .out12(write12), .out13(write13),
    .out14(write14), .out15(write15), .out16(write16), .out17(write17), .out18(write18), .out19(write19),
    .out20(write20), .out21(write21), .out22(write22), .out23(write23), .out24(write24), .out25(write25),
    .out26(write26), .out27(write27), .out28(write28), .out29(write29), .out30(write30), .out31(write31),
    .in(RegWEn), .sel(rd));  // open: out0
  // Probe on rd

  // Other names for the same wires on the sheet: outx1[31:0] = ra; outx2[31:0] = sp; outx5[31:0] = t0;
  //   outx6[31:0] = t1; outx7[31:0] = t2; outx8[31:0] = s0; outx9[31:0] = s1; outx10[31:0] = a0;
  //   read_data1[31:0] = Read_Data_1; read_data2[31:0] = Read_Data_2; read_reg1[4:0] = rs1; read_reg2[4:0] = rs2;
  //   write_en = RegWEn; write_reg[4:0] = rd

  // Notes on the sheet:
  //   INPUTS to your circuit
  //   DON'T CHANGE THE LOCATIONS OF THE INPUTS AND OUTPUTS!
  //   These are DEBUG/TEST outputs from your circuit.
  //   OUTPUTS from your circuit
endmodule

module regdatainput (
  input  [31:0] data_in,
  input  write_en,
  output [31:0] data_out,
  output writeflag
);


  assign data_out = data_in;
  assign writeflag = write_en;
endmodule
